// Logisim project e2380178.circ as structural Verilog: 1 circuit, main circuit main
module main (
  input  A0,
  input  A1,
  input  B0,
  input  B1,
  input  O0,
  input  O1,
  input  S,
  output E,
  output G,
  output L,
  output B,
  output N,
  output L0,
  output L1,
  output L2,
  output L3,
  output L4,
  output L5,
  output L6,
  output L7
);

  wire and_1_out, and_2_out, and_3_out, and_4_out, and_5_out, and_6_out, and_7_out, and_8_out, and_9_out,
       n3_to_8_decoder_74138_1_p5, n3_to_8_decoder_74138_1_p7, n3_to_8_decoder_74138_1_p8,
       n3_to_8_decoder_74138_1_p9, n3_to_8_decoder_74138_1_p10, n3_to_8_decoder_74138_1_p11,
       n3_to_8_decoder_74138_1_p12, n3_to_8_decoder_74138_1_p13, n3_to_8_decoder_74138_1_p14,
       n3_to_8_decoder_74138_2_p7, n3_to_8_decoder_74138_2_p8, n3_to_8_decoder_74138_2_p9,
       n3_to_8_decoder_74138_2_p10, n3_to_8_decoder_74138_2_p11, n3_to_8_decoder_74138_2_p12,
       n3_to_8_decoder_74138_2_p13, n3_to_8_decoder_74138_2_p14, n3_to_8_decoder_74138_3_p7,
       n3_to_8_decoder_74138_3_p8, n3_to_8_decoder_74138_3_p9, n3_to_8_decoder_74138_3_p10,
       n3_to_8_decoder_74138_3_p11, n3_to_8_decoder_74138_3_p12, n3_to_8_decoder_74138_3_p13,
       n3_to_8_decoder_74138_3_p14, n3_to_8_decoder_74138_3_p15, n4_to_1_mux_x2_74153_3_p7,
       n4_to_1_mux_x2_74153_3_p11, n4_to_1_mux_x2_74153_3_p12, n4_to_1_mux_x2_74153_4_p15,
       n4_to_1_mux_x2_74153_4_p16, nor_1_out, nor_2_out, not_2_out, not_3_out, not_4_out, not_5_out,
       not_6_out, not_7_out, not_9_out, not_10_out, not_11_out, not_12_out, not_13_out, not_14_out,
       not_15_out, not_16_out, not_17_out, not_18_out, not_19_out, not_20_out, not_21_out, not_22_out,
       not_23_out, not_25_out, not_26_out, not_27_out, not_28_out, not_29_out, not_31_out, not_33_out,
       not_34_out, not_35_out, not_36_out, not_37_out, not_38_out, not_39_out, not_40_out, or_1_out,
       or_2_out, or_3_out, or_4_out, or_5_out, or_6_out, or_7_out, or_8_out, or_10_out, or_12_out, or_13_out,
       or_15_out, xor_1_out, xor_2_out, xor_3_out;

  not not_1 (L7, 1'b1);
  or or_1 (or_1_out, A0, A1);
  and and_1 (and_1_out, A0, A1);
  xor xor_1 (xor_1_out, A0, B0);
  and and_2 (and_2_out, A0, B0);
  xor xor_2 (xor_2_out, A1, B1);
  and and_3 (and_3_out, A1, B1);
  nor nor_1 (nor_1_out, B0, B1);
  not not_2 (not_2_out, B1);
  not not_3 (not_3_out, B0);
  not not_4 (not_4_out, B0);
  not not_5 (not_5_out, or_1_out);
  not not_6 (not_6_out, A1);
  not not_7 (not_7_out, and_1_out);
  // _3_to_8_decoder__74138 #(.Facing("east")) 3_to_8_decoder_74138_1: pin names not known; wires that end beside it: O0, O1, S, 1'b1, n3_to_8_decoder_74138_1_p5, n3_to_8_decoder_74138_1_p5, n3_to_8_decoder_74138_1_p7, n3_to_8_decoder_74138_1_p8, n3_to_8_decoder_74138_1_p9, n3_to_8_decoder_74138_1_p10, n3_to_8_decoder_74138_1_p11, n3_to_8_decoder_74138_1_p12, n3_to_8_decoder_74138_1_p13, n3_to_8_decoder_74138_1_p14
  not not_8 (n3_to_8_decoder_74138_1_p5, 1'b1);
  not not_9 (not_9_out, A1);
  not not_10 (not_10_out, A0);
  not not_11 (not_11_out, A1);
  and and_4 (and_4_out, A0, A1);
  and and_5 (and_5_out, and_2_out, xor_2_out);
  and and_6 (and_6_out, B0, not_2_out);
  and and_7 (and_7_out, not_3_out, B1);
  and and_8 (and_8_out, B0, B1);
  not not_12 (not_12_out, n3_to_8_decoder_74138_1_p7);
  not not_13 (not_13_out, n3_to_8_decoder_74138_1_p8);
  not not_14 (not_14_out, n3_to_8_decoder_74138_1_p9);
  not not_15 (not_15_out, n3_to_8_decoder_74138_1_p10);
  not not_16 (not_16_out, n3_to_8_decoder_74138_1_p11);
  not not_17 (not_17_out, n3_to_8_decoder_74138_1_p12);
  not not_18 (not_18_out, n3_to_8_decoder_74138_1_p13);
  not not_19 (not_19_out, n3_to_8_decoder_74138_1_p14);
  and and_9 (and_9_out, not_10_out, not_11_out);
  not not_20 (not_20_out, and_4_out);
  xor xor_3 (xor_3_out, and_2_out, xor_2_out);
  or or_2 (or_2_out, and_5_out, and_3_out);
  not not_21 (not_21_out, not_19_out);
  or or_3 (or_3_out, not_18_out, not_14_out);
  or or_4 (or_4_out, not_12_out, not_16_out);
  not not_22 (not_22_out, or_4_out);
  // _4_to_1_MUX__x2___74153 #(.Facing("east")) 4_to_1_mux_x2_74153_1: pin names not known; wires that end beside it: or_1_out, A1, and_1_out, L7, L7, not_5_out, not_6_out, not_7_out, not_22_out, B0, not_22_out, B1, G, L
  not not_23 (not_23_out, or_5_out);
  or or_5 (or_5_out, not_13_out, not_17_out);
  // _4_to_1_MUX__x2___74153 #(.Facing("east")) 4_to_1_mux_x2_74153_2: pin names not known; wires that end beside it: A0, A1, A0, A1, L7, and_9_out, not_9_out, not_20_out, not_23_out, B0, not_21_out, B1, B, N
  // _3_to_8_decoder__74138 #(.Facing("east")) 3_to_8_decoder_74138_2: pin names not known; wires that end beside it: A0, A1, not_18_out, or_3_out, L7, L7, n3_to_8_decoder_74138_2_p7, n3_to_8_decoder_74138_2_p8, n3_to_8_decoder_74138_2_p9, n3_to_8_decoder_74138_2_p10, n3_to_8_decoder_74138_2_p11, n3_to_8_decoder_74138_2_p12, n3_to_8_decoder_74138_2_p13, n3_to_8_decoder_74138_2_p14
  // _3_to_8_decoder__74138 #(.Facing("east")) 3_to_8_decoder_74138_3: pin names not known; wires that end beside it: xor_1_out, xor_3_out, or_2_out, not_15_out, L7, L7, n3_to_8_decoder_74138_3_p7, n3_to_8_decoder_74138_3_p8, n3_to_8_decoder_74138_3_p9, n3_to_8_decoder_74138_3_p10, n3_to_8_decoder_74138_3_p11, n3_to_8_decoder_74138_3_p12, n3_to_8_decoder_74138_3_p13, n3_to_8_decoder_74138_3_p14, n3_to_8_decoder_74138_3_p15
  // _4_to_1_MUX__x2___74153 #(.Facing("east")) 4_to_1_mux_x2_74153_3: pin names not known; wires that end beside it: nor_1_out, and_6_out, and_7_out, and_8_out, and_6_out, not_4_out, n4_to_1_mux_x2_74153_3_p7, and_7_out, not_21_out, not_21_out, n4_to_1_mux_x2_74153_3_p11, n4_to_1_mux_x2_74153_3_p12
  not not_24 (n4_to_1_mux_x2_74153_3_p7, not_4_out);
  // _4_to_1_MUX__x2___74153 #(.Facing("east")) 4_to_1_mux_x2_74153_4: pin names not known; wires that end beside it: and_7_out, and_8_out, nor_1_out, and_6_out, and_8_out, L7, L7, nor_1_out, A0, not_21_out, A0, A1, not_21_out, A1, n4_to_1_mux_x2_74153_4_p15, n4_to_1_mux_x2_74153_4_p16
  not not_25 (not_25_out, n3_to_8_decoder_74138_3_p7);
  not not_26 (not_26_out, n3_to_8_decoder_74138_3_p8);
  not not_27 (not_27_out, n3_to_8_decoder_74138_3_p9);
  not not_28 (not_28_out, n3_to_8_decoder_74138_3_p10);
  not not_29 (not_29_out, n3_to_8_decoder_74138_3_p11);
  not not_30 (L5, n3_to_8_decoder_74138_3_p12);
  not not_31 (not_31_out, n3_to_8_decoder_74138_3_p13);
  not not_32 (n3_to_8_decoder_74138_3_p15, n3_to_8_decoder_74138_3_p14);
  or or_6 (or_6_out, not_12_out, not_16_out);
  nor nor_2 (nor_2_out, L, G);
  not not_33 (not_33_out, n3_to_8_decoder_74138_2_p7);
  not not_34 (not_34_out, n3_to_8_decoder_74138_2_p8);
  not not_35 (not_35_out, n3_to_8_decoder_74138_2_p9);
  not not_36 (not_36_out, n3_to_8_decoder_74138_2_p10);
  not not_37 (not_37_out, n3_to_8_decoder_74138_2_p11);
  not not_38 (not_38_out, n3_to_8_decoder_74138_2_p12);
  not not_39 (not_39_out, n3_to_8_decoder_74138_2_p13);
  not not_40 (not_40_out, n3_to_8_decoder_74138_2_p14);
  and and_10 (E, or_6_out, nor_2_out);
  or or_7 (or_7_out, not_33_out, not_34_out);
  or or_8 (or_8_out, not_35_out, not_36_out);
  or or_9 (L3, not_28_out, n4_to_1_mux_x2_74153_4_p16);
  or or_10 (or_10_out, or_7_out, not_37_out);
  or or_11 (L0, or_10_out, or_12_out);
  or or_12 (or_12_out, not_25_out, n4_to_1_mux_x2_74153_3_p11);
  or or_13 (or_13_out, or_8_out, n4_to_1_mux_x2_74153_3_p12);
  or or_14 (L1, or_13_out, not_26_out);
  or or_15 (or_15_out, not_38_out, not_27_out);
  or or_16 (L2, or_15_out, n4_to_1_mux_x2_74153_4_p15);
  or or_17 (L4, not_29_out, not_39_out);
  or or_18 (L6, not_31_out, not_40_out);
endmodule
